# Fritzing sketch Circuit (saved by Fritzing 0.9.3b)

parts:
  Componente1 = Arduino Mega Proto Shield
  Arduino_CNC_Shield_V3_00_1 = Arduino_CNC_V3.00
  U2 = RJ45 Jack [package=rj45-8]
  Mosfet_driver_module1 = IFR520 MOS module [package=THT]
  U5 = LM2596 step down module
  S1 = Limit Switch [package="Breakout Board"]
  S2 = Limit Switch [package="Breakout Board"]
  M1 = Stepper Motor - Bipolar
  LED1 = LED - 3W Aluminum PCB
  J1 = MAGJACK [package=magjack]
  J2 = MAGJACK [package=magjack]  # not connected

nets:
  N1: Componente1.D12, Mosfet_driver_module1.pin1
  N2: Componente1.D32, Arduino_CNC_Shield_V3_00_1.A.DIR
  N3: Componente1.D34, Arduino_CNC_Shield_V3_00_1.A.STEP
  N4: Componente1.D36, Arduino_CNC_Shield_V3_00_1.Z.DIR
  N5: Componente1.D38, Arduino_CNC_Shield_V3_00_1.Z.STEP
  N6: Componente1.D40, Arduino_CNC_Shield_V3_00_1.Y.DIR
  N7: Componente1.D42, Arduino_CNC_Shield_V3_00_1.Y.STEP
  N8: Componente1.D44, Arduino_CNC_Shield_V3_00_1.X.DIR
  N9: Componente1.D46, Arduino_CNC_Shield_V3_00_1.X.STEP
  N10: Componente1.5V, Componente1.N$381
  N11: Componente1.GND, Componente1.N$383
  N12: Componente1.5V@1, U2.1, U2.2
  N13: Componente1.N$413, U2.3, Mosfet_driver_module1.pin5
  N14: Componente1.N$424, Mosfet_driver_module1.pin3
  N15: Componente1.N$426, Mosfet_driver_module1.pin2
  N16: Arduino_CNC_Shield_V3_00_1.EN(able), Arduino_CNC_Shield_V3_00_1.GND
  N17: Arduino_CNC_Shield_V3_00_1.X-MTR_'1', U2.5
  N18: Arduino_CNC_Shield_V3_00_1.X-MTR_'2', U2.6
  N19: Arduino_CNC_Shield_V3_00_1.X-MTR_'3', U2.7
  N20: Arduino_CNC_Shield_V3_00_1.X-MTR_'4', U2.8
  N21: U2.4, Mosfet_driver_module1.pin4
  N22: Mosfet_driver_module1.pin6, U5.OUT+
  N23: Mosfet_driver_module1.pin7, U5.OUT-
  N24: S1.V, S2.G, J1.GLED+
  N25: S1.S, S2.S, J1.GLED-
  N26: M1.A, J1.TD-
  N27: M1.C, J1.TD+
  N28: M1.B, J1.TCT
  N29: LED1.anode, J1.YLED-
  N30: LED1.cathode, J1.YLED+

notes:
  const int StepX = 30;
  const int DirX = 31;
  const int StepY = 32;
  const int DirY = 33;
  const int StepZ = 34;
  const int DirZ = 35;
  const int StepZ = 36;
  const int DirZ = 37;

custom parts:
  Arduino_CNC_V3.00: Protoneer Arduino CNC Shield V3.00 If using Grbl V0.9: The “A” axis can not be used (yet). The “SCL” (Arduino A5) pin is now used for 'Probing' input. The “End Stops Z+ & Z-” (Arduino D11) and “SpnEn” (Arduino D12) have been switched!
  IFR520 MOS module: Breakout board for the IFR520 MOSFET transistor. The module is designed to switch heavy DC loads from a single digital pin of your microcontroller. Its main purpose is to provide a low cost way to drive a DC motor for robotics applications, but the module can be used to control most high current DC loads. Screw terminals are provided to interface to your load and external power source. An LED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
  LM2596 step down module: LM2596 DC-DC step down power supply module 3 A.
  Limit Switch: Generic limit switch commonly found on 3D printers. Typical lever microswitch mounted on a PCB board with a 3 pin JST XH connector.
  LED - 3W Aluminum PCB: Description: So much power and light from such a small package. This 5 pack of red 3 Watt aluminum backed PCBs is sure to shed a lot of light on any project you add it to. These LEDs act as any other LED except these little guys require much more power while delivering a light as intense of a thousand suns going super nova (this is an exaggeration but you know what we mean)! Each LED in the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
